// Logisim project Project.circ as structural Verilog: 2 circuits, main circuit FillAdder
module main (
  input  in_1,
  input  in_2,
  input  in_3,
  input  in_4,
  input  in_5,
  input  in_6,
  input  in_7,
  input  L_Initial_Value,
  input  in_9,
  input  in_10,
  input  in_11,
  input  in_12,
  input  in_13,
  input  in_14,
  output Zero,
  output Negative,
  output Overflow,
  output SignedOverflow,
  output Zero_2,
  output Negative_2,
  output Overflow_2,
  output out_22,
  output out_23,
  output out_24,
  output out_25
);

  wire and_1_out, and_2_out, and_3_out, and_4_out, and_5_out, and_6_out, and_7_out, and_8_out, and_9_out,
       and_10_out, and_11_out, and_12_out, and_13_out, and_14_out, and_15_out, and_16_out, and_17_out,
       and_18_out, and_19_out, and_20_out, and_21_out, and_22_out, and_23_out, and_24_out, and_25_out,
       and_26_out, and_27_out, and_28_out, and_29_out, and_30_out, and_31_out, and_32_out, and_33_out,
       and_34_out, and_35_out, and_36_out, and_37_out, and_38_out, and_39_out, and_40_out, and_41_out,
       and_42_out, and_43_out, and_44_out, and_45_out, and_46_out, and_47_out, and_48_out, and_49_out,
       and_50_out, and_51_out, and_53_out, and_54_out, and_55_out, and_56_out, and_57_out, and_58_out,
       and_59_out, and_60_out, and_61_out, and_62_out, and_63_out, and_64_out, and_65_out, and_66_out,
       and_67_out, and_68_out, and_69_out, and_70_out, and_71_out, and_72_out, and_73_out, and_74_out,
       and_75_out, and_76_out, and_77_out, and_78_out, and_79_out, and_80_out, and_81_out, and_82_out,
       and_83_out, and_84_out, and_85_out, and_86_out, and_87_out, and_88_out, and_89_out, and_90_out,
       and_91_out, and_92_out, and_93_out, and_94_out, and_95_out, and_96_out, and_97_out, and_98_out,
       and_99_out, and_100_out, and_101_out, and_102_out, and_103_out, and_104_out, and_105_out, and_107_out,
       and_108_out, and_109_out, and_110_out, and_111_out, and_112_out, and_113_out, and_114_out,
       and_115_out, and_116_out, and_117_out, and_118_out, and_119_out, and_120_out, and_121_out,
       and_122_out, and_123_out, and_124_out, and_125_out, and_126_out, and_127_out, and_128_out,
       and_129_out, and_130_out, and_131_out, and_132_out, and_133_out, and_134_out, and_135_out,
       and_136_out, and_137_out, and_138_out, and_139_out, and_140_out, and_141_out, and_142_out,
       and_143_out, and_144_out, and_145_out, and_147_out, and_148_out, and_149_out, and_150_out,
       and_151_out, and_152_out, and_153_out, and_154_out, and_156_out, and_157_out, and_158_out,
       and_159_out, and_160_out, and_161_out, and_162_out, and_163_out, clock_1_out, d_ff_1_q, d_ff_2_q,
       d_ff_3_q, d_ff_4_q, d_ff_5_q, d_ff_6_q, d_ff_7_q, d_ff_8_q, d_ff_9_q, d_ff_10_q, d_ff_11_q, d_ff_12_q,
       d_ff_13_q, d_ff_14_q, d_ff_15_q, d_ff_16_q, d_ff_17_q, d_ff_18_q, d_ff_19_q, d_ff_20_q, d_ff_21_q,
       d_ff_22_q, d_ff_23_q, d_ff_24_q, d_ff_25_q, d_ff_26_q, d_ff_27_q, d_ff_28_q, d_ff_29_q, d_ff_30_q,
       d_ff_31_q, d_ff_32_q, d_ff_33_q, d_ff_34_q, d_ff_35_q, d_ff_38_q, d_ff_38_qn, d_ff_47_q, d_ff_48_q,
       d_ff_51_q, d_ff_52_q, d_ff_53_q, d_ff_54_q, d_ff_55_q, d_ff_56_q, decoder_1_out0, decoder_1_out1,
       decoder_1_out2, decoder_1_out3, decoder_1_out4, decoder_1_out5, decoder_1_out6, decoder_1_out7,
       decoder_1_out8, decoder_1_out9, decoder_1_out10, decoder_1_out11, decoder_1_out12, decoder_1_out13,
       decoder_1_out14, decoder_1_out15, filladder_1_c, filladder_2_c, filladder_3_c, filladder_4_c,
       filladder_5_c, filladder_5_sum, filladder_6_c, filladder_6_sum, multiplexer_1_out, multiplexer_2_out,
       multiplexer_3_out, multiplexer_4_out, multiplexer_6_out, multiplexer_7_out, multiplexer_8_out,
       multiplexer_9_out, multiplexer_10_out, multiplexer_11_out, multiplexer_12_out, multiplexer_13_out,
       multiplexer_14_out, multiplexer_16_out, multiplexer_17_out, multiplexer_18_out, Neg_2_out, Neg_out,
       not_1_out, not_2_out, not_3_out, not_4_out, not_5_out, not_6_out, not_7_out, not_8_out, not_9_out,
       not_10_out, not_11_out, not_12_out, not_13_out, not_14_out, not_15_out, not_16_out, not_17_out,
       not_18_out, not_19_out, not_20_out, not_21_out, not_22_out, not_23_out, not_24_out, not_25_out,
       not_26_out, not_27_out, not_28_out, not_29_out, not_30_out, not_31_out, not_32_out, not_33_out,
       not_34_out, not_35_out, not_36_out, not_37_out, not_38_out, not_39_out, not_40_out, not_41_out,
       not_42_out, not_43_out, not_44_out, not_45_out, not_46_out, not_47_out, not_48_out, not_49_out,
       not_50_out, not_51_out, not_52_out, or_1_out, or_2_out, or_3_out, or_4_out, or_5_out, or_6_out,
       or_7_out, or_8_out, or_9_out, or_10_out, or_11_out, or_12_out, or_13_out, or_14_out, or_15_out,
       or_16_out, or_17_out, or_18_out, or_19_out, or_20_out, or_21_out, or_22_out, or_23_out, or_24_out,
       or_25_out, or_26_out, or_27_out, or_28_out, or_29_out, or_30_out, or_31_out, or_32_out, or_33_out,
       or_34_out, or_35_out, or_36_out, Pos_2_out, Pos_out, xor_2_out, xor_3_out, xor_4_out, xor_5_out,
       xor_6_out, xor_7_out, xor_8_out, xor_9_out, xor_10_out;
  wire [3:0] d_ff_40_q, d_ff_49_q, d_ff_50_q, multiplexer_5_out, multiplexer_15_out;

  Clock clock_1 (.out(clock_1_out));
  not not_1 (not_1_out, d_ff_11_q);
  not not_2 (not_2_out, d_ff_2_q);
  not not_3 (not_3_out, d_ff_2_q);
  not not_4 (not_4_out, d_ff_11_q);
  not not_5 (not_5_out, d_ff_1_q);
  not not_6 (not_6_out, d_ff_1_q);
  not not_7 (not_7_out, d_ff_11_q);
  not not_8 (not_8_out, d_ff_1_q);
  not not_9 (not_9_out, d_ff_2_q);
  not not_10 (not_10_out, d_ff_1_q);
  not not_11 (not_11_out, d_ff_2_q);
  not not_12 (not_12_out, d_ff_11_q);
  and and_1 (and_1_out, d_ff_1_q, d_ff_2_q, clock_1_out, d_ff_11_q);
  and and_2 (and_2_out, d_ff_1_q, d_ff_2_q, clock_1_out, not_1_out);
  and and_3 (and_3_out, d_ff_1_q, not_2_out, clock_1_out, d_ff_11_q);
  and and_4 (and_4_out, d_ff_1_q, not_3_out, clock_1_out, not_4_out);
  and and_5 (and_5_out, not_5_out, d_ff_2_q, clock_1_out, d_ff_11_q);
  and and_6 (and_6_out, not_6_out, d_ff_2_q, clock_1_out, not_7_out);
  and and_7 (and_7_out, not_8_out, not_9_out, clock_1_out, d_ff_11_q);
  and and_8 (and_8_out, not_10_out, not_11_out, clock_1_out, not_12_out);
  D_Flip_Flop #(.trigger("falling")) d_ff_1 (.D(out_23), .clk(clock_1_out), .Q(d_ff_1_q));  // open: Qn, preset, reset
  and and_9 (and_9_out, and_1_out, not_13_out);
  and and_10 (and_10_out, and_2_out, not_13_out);
  and and_11 (and_11_out, and_3_out, not_13_out);
  and and_12 (and_12_out, and_4_out, not_13_out);
  and and_13 (and_13_out, and_5_out, not_13_out);
  and and_14 (and_14_out, and_6_out, not_13_out);
  and and_15 (and_15_out, and_7_out, not_13_out);
  and and_16 (and_16_out, and_8_out, not_13_out);
  not not_13 (not_13_out, in_1);
  D_Flip_Flop #(.trigger("falling")) d_ff_2 (.D(out_24), .clk(clock_1_out), .Q(d_ff_2_q));  // open: Qn, preset, reset
  D_Flip_Flop #(.trigger("high")) d_ff_3 (.D(and_17_out), .clk(and_9_out), .Q(d_ff_3_q));  // open: Qn, preset, reset
  and and_17 (and_17_out, and_1_out, not_13_out, in_2);
  and and_18 (and_18_out, and_2_out, not_13_out, in_2);
  D_Flip_Flop #(.trigger("high")) d_ff_4 (.D(and_18_out), .clk(and_10_out), .Q(d_ff_4_q));  // open: Qn, preset, reset
  and and_19 (and_19_out, and_3_out, not_13_out, in_2);
  D_Flip_Flop #(.trigger("high")) d_ff_5 (.D(and_19_out), .clk(and_11_out), .Q(d_ff_5_q));  // open: Qn, preset, reset
  D_Flip_Flop #(.trigger("high")) d_ff_6 (.D(and_20_out), .clk(and_12_out), .Q(d_ff_6_q));  // open: Qn, preset, reset
  and and_20 (and_20_out, and_4_out, not_13_out, in_2);
  and and_21 (and_21_out, and_5_out, not_13_out, in_2);
  D_Flip_Flop #(.trigger("high")) d_ff_7 (.D(and_21_out), .clk(and_13_out), .Q(d_ff_7_q));  // open: Qn, preset, reset
  and and_22 (and_22_out, and_6_out, not_13_out, in_2);
  D_Flip_Flop #(.trigger("high")) d_ff_8 (.D(and_22_out), .clk(and_14_out), .Q(d_ff_8_q));  // open: Qn, preset, reset
  and and_23 (and_23_out, and_7_out, not_13_out, in_2);
  D_Flip_Flop #(.trigger("high")) d_ff_9 (.D(and_23_out), .clk(and_15_out), .Q(d_ff_9_q));  // open: Qn, preset, reset
  and and_24 (and_24_out, and_8_out, not_13_out, in_2);
  D_Flip_Flop #(.trigger("high")) d_ff_10 (.D(and_24_out), .clk(and_16_out), .Q(d_ff_10_q));  // open: Qn, preset, reset
  D_Flip_Flop #(.trigger("falling")) d_ff_11 (.D(out_25), .clk(clock_1_out), .Q(d_ff_11_q));  // open: Qn, preset, reset
  or or_1 (or_1_out, and_25_out, and_26_out, and_27_out, and_28_out, and_29_out, and_30_out, and_31_out, and_32_out);
  and and_25 (and_25_out, d_ff_3_q, and_1_out, in_1);
  and and_26 (and_26_out, d_ff_4_q, and_2_out, in_1);
  and and_27 (and_27_out, d_ff_5_q, and_3_out, in_1);
  and and_28 (and_28_out, d_ff_6_q, and_4_out, in_1);
  and and_29 (and_29_out, d_ff_7_q, and_5_out, in_1);
  and and_30 (and_30_out, d_ff_8_q, and_6_out, in_1);
  and and_31 (and_31_out, d_ff_9_q, and_7_out, in_1);
  and and_32 (and_32_out, d_ff_10_q, and_8_out, in_1);
  and and_33 (and_33_out, clock_1_out, in_7);
  not not_14 (not_14_out, in_14);
  and and_34 (and_34_out, and_1_out, not_13_out, in_3);
  D_Flip_Flop #(.trigger("high")) d_ff_12 (.D(and_34_out), .clk(and_9_out), .Q(d_ff_12_q));  // open: Qn, preset, reset
  D_Flip_Flop #(.trigger("high")) d_ff_13 (.D(and_35_out), .clk(and_10_out), .Q(d_ff_13_q));  // open: Qn, preset, reset
  and and_35 (and_35_out, and_2_out, not_13_out, in_3);
  and and_36 (and_36_out, and_3_out, not_13_out, in_3);
  D_Flip_Flop #(.trigger("high")) d_ff_14 (.D(and_36_out), .clk(and_11_out), .Q(d_ff_14_q));  // open: Qn, preset, reset
  and and_37 (and_37_out, and_4_out, not_13_out, in_3);
  D_Flip_Flop #(.trigger("high")) d_ff_15 (.D(and_37_out), .clk(and_12_out), .Q(d_ff_15_q));  // open: Qn, preset, reset
  and and_38 (and_38_out, and_5_out, not_13_out, in_3);
  D_Flip_Flop #(.trigger("high")) d_ff_16 (.D(and_38_out), .clk(and_13_out), .Q(d_ff_16_q));  // open: Qn, preset, reset
  and and_39 (and_39_out, and_6_out, not_13_out, in_3);
  D_Flip_Flop #(.trigger("high")) d_ff_17 (.D(and_39_out), .clk(and_14_out), .Q(d_ff_17_q));  // open: Qn, preset, reset
  D_Flip_Flop #(.trigger("high")) d_ff_18 (.D(and_40_out), .clk(and_15_out), .Q(d_ff_18_q));  // open: Qn, preset, reset
  and and_40 (and_40_out, and_7_out, not_13_out, in_3);
  and and_41 (and_41_out, and_8_out, not_13_out, in_3);
  D_Flip_Flop #(.trigger("high")) d_ff_19 (.D(and_41_out), .clk(and_16_out), .Q(d_ff_19_q));  // open: Qn, preset, reset
  and and_42 (and_42_out, clock_1_out, d_ff_1_q);
  or or_2 (or_2_out, and_42_out, L_Initial_Value);
  FillAdder filladder_1 (.A(or_7_out), .B(and_33_out), .Carry(filladder_2_c), .C(filladder_1_c), .Sum(Negative_2));
  and and_43 (and_43_out, d_ff_12_q, and_1_out, in_1);
  and and_44 (and_44_out, d_ff_13_q, and_2_out, in_1);
  and and_45 (and_45_out, d_ff_14_q, and_3_out, in_1);
  and and_46 (and_46_out, d_ff_15_q, and_4_out, in_1);
  and and_47 (and_47_out, d_ff_16_q, and_5_out, in_1);
  and and_48 (and_48_out, d_ff_17_q, and_6_out, in_1);
  and and_49 (and_49_out, d_ff_18_q, and_7_out, in_1);
  and and_50 (and_50_out, d_ff_19_q, and_8_out, in_1);
  and and_51 (and_51_out, clock_1_out, d_ff_2_q);
  or or_3 (or_3_out, and_51_out, in_9);
  FillAdder filladder_2 (.A(or_6_out), .B(or_2_out), .Carry(filladder_3_c), .C(filladder_2_c), .Sum(out_23));
  or or_4 (or_4_out, and_43_out, and_44_out, and_45_out, and_46_out, and_47_out, and_48_out, and_49_out, and_50_out);
  // AND_Gate and_52 has open pins: in0=clock_1_out, out=open
  and and_53 (and_53_out, clock_1_out, d_ff_11_q);
  or or_5 (or_5_out, and_53_out, in_10);
  FillAdder filladder_3 (.A(or_8_out), .B(or_3_out), .Carry(and_54_out), .C(filladder_3_c), .Sum(out_24));
  or or_6 (or_6_out, xor_3_out, and_72_out);
  or or_7 (or_7_out, xor_2_out, and_71_out);
  and and_54 (and_54_out, or_5_out, or_9_out);
  and and_55 (and_55_out, and_1_out, not_13_out, in_4);
  D_Flip_Flop #(.trigger("high")) d_ff_20 (.D(and_55_out), .clk(and_9_out), .Q(d_ff_20_q));  // open: Qn, preset, reset
  and and_56 (and_56_out, and_2_out, not_13_out, in_4);
  D_Flip_Flop #(.trigger("high")) d_ff_21 (.D(and_56_out), .clk(and_10_out), .Q(d_ff_21_q));  // open: Qn, preset, reset
  D_Flip_Flop #(.trigger("high")) d_ff_22 (.D(and_57_out), .clk(and_11_out), .Q(d_ff_22_q));  // open: Qn, preset, reset
  and and_57 (and_57_out, and_3_out, not_13_out, in_4);
  and and_58 (and_58_out, and_4_out, not_13_out, in_4);
  D_Flip_Flop #(.trigger("high")) d_ff_23 (.D(and_58_out), .clk(and_12_out), .Q(d_ff_23_q));  // open: Qn, preset, reset
  D_Flip_Flop #(.trigger("high")) d_ff_24 (.D(and_59_out), .clk(and_13_out), .Q(d_ff_24_q));  // open: Qn, preset, reset
  and and_59 (and_59_out, and_5_out, not_13_out, in_4);
  and and_60 (and_60_out, and_6_out, not_13_out, in_4);
  D_Flip_Flop #(.trigger("high")) d_ff_25 (.D(and_60_out), .clk(and_14_out), .Q(d_ff_25_q));  // open: Qn, preset, reset
  and and_61 (and_61_out, and_7_out, not_13_out, in_4);
  D_Flip_Flop #(.trigger("high")) d_ff_26 (.D(and_61_out), .clk(and_15_out), .Q(d_ff_26_q));  // open: Qn, preset, reset
  D_Flip_Flop #(.trigger("high")) d_ff_27 (.D(and_62_out), .clk(and_16_out), .Q(d_ff_27_q));  // open: Qn, preset, reset
  and and_62 (and_62_out, and_8_out, not_13_out, in_4);
  or or_8 (or_8_out, xor_4_out, and_75_out);
  or or_9 (or_9_out, xor_5_out, and_74_out);
  xor xor_1 (out_25, or_5_out, or_9_out);
  or or_10 (or_10_out, and_63_out, and_64_out, and_65_out, and_66_out, and_67_out, and_68_out, and_69_out, and_70_out);
  and and_63 (and_63_out, d_ff_20_q, and_1_out, in_1);
  and and_64 (and_64_out, d_ff_21_q, and_2_out, in_1);
  and and_65 (and_65_out, d_ff_22_q, and_3_out, in_1);
  and and_66 (and_66_out, d_ff_23_q, and_4_out, in_1);
  and and_67 (and_67_out, d_ff_24_q, and_5_out, in_1);
  and and_68 (and_68_out, d_ff_25_q, and_6_out, in_1);
  and and_69 (and_69_out, d_ff_26_q, and_7_out, in_1);
  and and_70 (and_70_out, d_ff_27_q, and_8_out, in_1);
  and and_71 (and_71_out, and_87_out, not_14_out);
  and and_72 (and_72_out, and_88_out, not_14_out);
  and and_73 (and_73_out, not_19_out, and_76_out);
  xor xor_2 (xor_2_out, not_19_out, and_76_out);
  not not_15 (not_15_out, out_25);
  not not_16 (not_16_out, out_24);
  not not_17 (not_17_out, out_23);
  not not_18 (not_18_out, Negative_2);
  and and_74 (and_74_out, and_100_out, not_14_out);
  and and_75 (and_75_out, and_86_out, not_14_out);
  xor xor_3 (xor_3_out, not_20_out, and_91_out);
  and and_76 (and_76_out, not_20_out, and_91_out);
  and and_77 (and_77_out, not_15_out, not_16_out, not_17_out, not_18_out);
  and and_78 (and_78_out, and_1_out, not_13_out, in_5);
  D_Flip_Flop #(.trigger("high")) d_ff_28 (.D(and_78_out), .clk(and_9_out), .Q(d_ff_28_q));  // open: Qn, preset, reset
  and and_79 (and_79_out, and_2_out, not_13_out, in_5);
  D_Flip_Flop #(.trigger("high")) d_ff_29 (.D(and_79_out), .clk(and_10_out), .Q(d_ff_29_q));  // open: Qn, preset, reset
  D_Flip_Flop #(.trigger("high")) d_ff_30 (.D(and_80_out), .clk(and_11_out), .Q(d_ff_30_q));  // open: Qn, preset, reset
  and and_80 (and_80_out, and_3_out, not_13_out, in_5);
  and and_81 (and_81_out, and_4_out, not_13_out, in_5);
  D_Flip_Flop #(.trigger("high")) d_ff_31 (.D(and_81_out), .clk(and_12_out), .Q(d_ff_31_q));  // open: Qn, preset, reset
  D_Flip_Flop #(.trigger("high")) d_ff_32 (.D(and_82_out), .clk(and_13_out), .Q(d_ff_32_q));  // open: Qn, preset, reset
  and and_82 (and_82_out, and_5_out, not_13_out, in_5);
  D_Flip_Flop #(.trigger("high")) d_ff_33 (.D(and_83_out), .clk(and_14_out), .Q(d_ff_33_q));  // open: Qn, preset, reset
  and and_83 (and_83_out, and_6_out, not_13_out, in_5);
  D_Flip_Flop #(.trigger("high")) d_ff_34 (.D(and_84_out), .clk(and_15_out), .Q(d_ff_34_q));  // open: Qn, preset, reset
  and and_84 (and_84_out, and_7_out, not_13_out, in_5);
  and and_85 (and_85_out, and_8_out, not_13_out, in_5);
  D_Flip_Flop #(.trigger("high")) d_ff_35 (.D(and_85_out), .clk(and_16_out), .Q(d_ff_35_q));  // open: Qn, preset, reset
  and and_86 (and_86_out, in_13, clock_1_out);
  and and_87 (and_87_out, in_11, clock_1_out);
  and and_88 (and_88_out, in_12, clock_1_out);
  and and_89 (and_89_out, and_87_out, in_14);
  and and_90 (and_90_out, and_88_out, in_14);
  not not_19 (not_19_out, and_89_out);
  not not_20 (not_20_out, and_90_out);
  and and_91 (and_91_out, not_26_out, and_103_out);
  xor xor_4 (xor_4_out, not_26_out, and_103_out);
  not not_21 (not_21_out, or_7_out);
  not not_22 (not_22_out, and_33_out);
  not not_23 (not_23_out, or_7_out);
  or or_11 (or_11_out, and_92_out, and_93_out, and_94_out, and_95_out, and_96_out, and_97_out, and_98_out, and_99_out);
  and and_92 (and_92_out, d_ff_28_q, and_1_out, in_1);
  and and_93 (and_93_out, d_ff_29_q, and_2_out, in_1);
  and and_94 (and_94_out, d_ff_30_q, and_3_out, in_1);
  and and_95 (and_95_out, d_ff_31_q, and_4_out, in_1);
  and and_96 (and_96_out, d_ff_32_q, and_5_out, in_1);
  and and_97 (and_97_out, d_ff_33_q, and_6_out, in_1);
  and and_98 (and_98_out, d_ff_34_q, and_7_out, in_1);
  and and_99 (and_99_out, d_ff_35_q, and_8_out, in_1);
  or or_12 (or_12_out, in_6, not_30_out, decoder_1_out15);
  not not_24 (not_24_out, or_12_out);
  and and_100 (and_100_out, not_24_out, clock_1_out);
  and and_101 (and_101_out, and_86_out, in_14);
  and and_102 (and_102_out, and_100_out, in_14);
  not not_25 (not_25_out, and_102_out);
  not not_26 (not_26_out, and_101_out);
  and and_103 (and_103_out, not_25_out, 1'b1);
  and and_104 (and_104_out, Negative_2, Neg_out);
  and Neg (Neg_out, or_7_out, and_33_out);
  and Pos (Pos_out, not_21_out, not_22_out);
  and and_105 (and_105_out, Pos_out, Negative_2);
  not not_27 (not_27_out, not_14_out);
  and and_106 (Zero_2, and_77_out, clock_1_out);
  and and_107 (and_107_out, in_1, clock_1_out);
  xor xor_5 (xor_5_out, not_25_out, 1'b1);
  or or_13 (or_13_out, and_108_out, and_105_out, and_109_out);
  and and_108 (and_108_out, not_27_out, not_23_out, filladder_1_c);
  D_Flip_Flop #(.trigger("falling")) d_ff_36 (
    .D(or_1_out), .clk(clock_1_out), .Q(d_ff_40_q[3]));  // open: Qn, preset, reset
  not not_28 (not_28_out, filladder_1_c);
  and and_109 (and_109_out, and_104_out, not_28_out);
  not not_29 (not_29_out, Zero_2);
  and notZero (Overflow_2, or_13_out, not_29_out);
  D_Flip_Flop #(.trigger("falling")) d_ff_37 (
    .D(or_4_out), .clk(clock_1_out), .Q(d_ff_40_q[2]));  // open: Qn, preset, reset
  D_Flip_Flop #(.trigger("falling")) d_ff_38 (
    .D(d_ff_38_qn), .clk(and_107_out), .Q(d_ff_38_q), .Qn(d_ff_38_qn));  // open: preset, reset
  D_Flip_Flop #(.trigger("falling")) d_ff_39 (
    .D(or_10_out), .clk(clock_1_out), .Q(d_ff_40_q[1]));  // open: Qn, preset, reset
  Decoder #(.select(4)) decoder_1 (
    .out0(decoder_1_out0), .out1(decoder_1_out1), .out2(decoder_1_out2), .out3(decoder_1_out3),
    .out4(decoder_1_out4), .out5(decoder_1_out5), .out6(decoder_1_out6), .out7(decoder_1_out7),
    .out8(decoder_1_out8), .out9(decoder_1_out9), .out10(decoder_1_out10), .out11(decoder_1_out11),
    .out12(decoder_1_out12), .out13(decoder_1_out13), .out14(decoder_1_out14), .out15(decoder_1_out15),
    .sel(d_ff_40_q), .en(and_110_out));
  and and_110 (and_110_out, in_1, d_ff_38_q);
  not not_30 (not_30_out, d_ff_38_q);
  D_Flip_Flop #(.trigger("falling")) d_ff_40 (
    .D(or_11_out), .clk(clock_1_out), .Q(d_ff_40_q[0]));  // open: Qn, preset, reset
  or or_14 (or_14_out, or_15_out, or_17_out);
  or or_15 (or_15_out, decoder_1_out12, decoder_1_out13, decoder_1_out9, decoder_1_out8);
  or or_16 (or_16_out, or_15_out, or_21_out);
  or or_17 (or_17_out, decoder_1_out14, decoder_1_out11, decoder_1_out10);
  or or_18 (or_18_out, or_17_out, or_22_out);
  and and_111 (and_111_out, or_16_out, clock_1_out);
  or or_19 (or_19_out, decoder_1_out4, decoder_1_out5);
  or or_20 (or_20_out, decoder_1_out6, decoder_1_out7);
  or or_21 (or_21_out, decoder_1_out1, decoder_1_out0);
  or or_22 (or_22_out, decoder_1_out3, decoder_1_out2);
  and and_112 (and_112_out, or_18_out, clock_1_out);
  and and_113 (and_113_out, clock_1_out, or_18_out);
  and and_114 (and_114_out, clock_1_out, or_16_out);
  or or_23 (or_23_out, decoder_1_out5, decoder_1_out4);
  not not_31 (not_31_out, or_23_out);
  Multiplexer #(.enable("false")) multiplexer_1 (
    .in0(d_ff_50_q[3]), .in1(multiplexer_6_out), .out(multiplexer_1_out), .sel(and_111_out));
  or or_24 (or_24_out, decoder_1_out7, decoder_1_out5, decoder_1_out3, decoder_1_out1);
  Multiplexer #(.enable("false")) multiplexer_2 (
    .in0(d_ff_50_q[2]), .in1(multiplexer_8_out), .out(multiplexer_2_out), .sel(and_111_out));
  not not_32 (not_32_out, or_15_out);
  or or_25 (or_25_out, decoder_1_out7, decoder_1_out6, decoder_1_out5, decoder_1_out4, decoder_1_out3, decoder_1_out2, decoder_1_out1, decoder_1_out0);
  or or_26 (or_26_out, decoder_1_out6, decoder_1_out4, decoder_1_out2, decoder_1_out0);
  Multiplexer #(.enable("false")) multiplexer_3 (
    .in0(d_ff_50_q[1]), .in1(multiplexer_10_out), .out(multiplexer_3_out), .sel(and_111_out));
  not not_33 (not_33_out, d_ff_40_q[2]);
  FillAdder filladder_4 (.A(or_28_out), .B(and_117_out), .Carry(filladder_5_c), .C(filladder_4_c), .Sum(Negative));
  or or_27 (or_27_out, decoder_1_out3, decoder_1_out2, decoder_1_out1, decoder_1_out0);
  Multiplexer #(.enable("false")) multiplexer_4 (
    .in0(d_ff_50_q[0]), .in1(multiplexer_12_out), .out(multiplexer_4_out), .sel(and_111_out));
  Multiplexer #(.width(4), .enable("false")) multiplexer_5 (
    .in0(d_ff_50_q), .in1(d_ff_49_q), .out(multiplexer_5_out), .sel(not_32_out));
  and and_115 (and_115_out, multiplexer_5_out[1], or_14_out);
  and and_116 (and_116_out, multiplexer_5_out[2], or_14_out);
  and and_117 (and_117_out, multiplexer_5_out[3], or_14_out);
  not not_34 (not_34_out, or_25_out);
  Multiplexer #(.enable("false")) multiplexer_6 (
    .in0(or_32_out), .in1(Negative), .out(multiplexer_6_out), .sel(not_34_out));
  Multiplexer #(.enable("false")) multiplexer_7 (
    .in0(d_ff_49_q[3]), .in1(multiplexer_6_out), .out(multiplexer_7_out), .sel(and_112_out));
  D_Flip_Flop #(.trigger("falling")) d_ff_41 (
    .D(multiplexer_7_out), .clk(and_113_out), .Q(d_ff_49_q[3]));  // open: Qn, preset, reset
  D_Flip_Flop #(.trigger("falling")) d_ff_42 (
    .D(multiplexer_1_out), .clk(and_114_out), .Q(d_ff_50_q[3]));  // open: Qn, preset, reset
  and and_118 (and_118_out, multiplexer_5_out[0], or_14_out);
  FillAdder filladder_5 (
    .A(or_30_out), .B(and_116_out), .Carry(filladder_6_c), .C(filladder_5_c), .Sum(filladder_5_sum));
  and and_119 (and_119_out, or_25_out, clock_1_out);
  Multiplexer #(.enable("false")) multiplexer_8 (
    .in0(or_33_out), .in1(filladder_5_sum), .out(multiplexer_8_out), .sel(not_34_out));
  Multiplexer #(.enable("false")) multiplexer_9 (
    .in0(d_ff_49_q[2]), .in1(multiplexer_8_out), .out(multiplexer_9_out), .sel(and_112_out));
  D_Flip_Flop #(.trigger("falling")) d_ff_43 (
    .D(multiplexer_9_out), .clk(and_113_out), .Q(d_ff_49_q[2]));  // open: Qn, preset, reset
  D_Flip_Flop #(.trigger("falling")) d_ff_44 (
    .D(multiplexer_2_out), .clk(and_114_out), .Q(d_ff_50_q[2]));  // open: Qn, preset, reset
  or or_28 (or_28_out, xor_7_out, and_125_out);
  FillAdder filladder_6 (.A(or_29_out), .B(and_115_out), .Carry(and_124_out), .C(filladder_6_c), .Sum(filladder_6_sum));
  and and_120 (and_120_out, and_119_out, or_24_out);
  and and_121 (and_121_out, and_120_out, not_35_out);
  and and_122 (and_122_out, and_119_out, or_26_out);
  and and_123 (and_123_out, and_122_out, not_35_out);
  Multiplexer #(.enable("false")) multiplexer_10 (
    .in0(or_35_out), .in1(filladder_6_sum), .out(multiplexer_10_out), .sel(not_34_out));
  Multiplexer #(.enable("false")) multiplexer_11 (
    .in0(d_ff_49_q[1]), .in1(multiplexer_10_out), .out(multiplexer_11_out), .sel(and_112_out));
  D_Flip_Flop #(.trigger("falling")) d_ff_45 (
    .D(multiplexer_11_out), .clk(and_113_out), .Q(d_ff_49_q[1]));  // open: Qn, preset, reset
  or or_29 (or_29_out, xor_9_out, and_129_out);
  or or_30 (or_30_out, xor_8_out, and_130_out);
  and and_124 (and_124_out, and_118_out, or_31_out);
  xor xor_6 (xor_6_out, and_118_out, or_31_out);
  not not_35 (not_35_out, or_27_out);
  Multiplexer #(.enable("false")) multiplexer_12 (
    .in0(or_36_out), .in1(xor_6_out), .out(multiplexer_12_out), .sel(not_34_out));
  Multiplexer #(.enable("false")) multiplexer_13 (
    .in0(d_ff_49_q[0]), .in1(multiplexer_12_out), .out(multiplexer_13_out), .sel(and_112_out));
  D_Flip_Flop #(.trigger("falling")) d_ff_46 (
    .D(multiplexer_3_out), .clk(and_114_out), .Q(d_ff_50_q[1]));  // open: Qn, preset, reset
  and and_125 (and_125_out, and_135_out, not_33_out);
  and and_126 (and_126_out, not_41_out, and_131_out);
  or or_31 (or_31_out, xor_10_out, and_138_out);
  not not_36 (not_36_out, xor_6_out);
  not not_37 (not_37_out, filladder_6_sum);
  not not_38 (not_38_out, filladder_5_sum);
  not not_39 (not_39_out, Negative);
  and and_127 (and_127_out, and_120_out, not_35_out, multiplexer_14_out);
  D_Flip_Flop #(.trigger("high")) d_ff_47 (
    .D(and_127_out), .clk(and_121_out), .Q(d_ff_47_q));  // open: Qn, preset, reset
  and and_128 (and_128_out, and_122_out, not_35_out, multiplexer_14_out);
  D_Flip_Flop #(.trigger("high")) d_ff_48 (
    .D(and_128_out), .clk(and_123_out), .Q(d_ff_48_q));  // open: Qn, preset, reset
  D_Flip_Flop #(.trigger("falling")) d_ff_49 (
    .D(multiplexer_13_out), .clk(and_113_out), .Q(d_ff_49_q[0]));  // open: Qn, preset, reset
  D_Flip_Flop #(.trigger("falling")) d_ff_50 (
    .D(multiplexer_4_out), .clk(and_114_out), .Q(d_ff_50_q[0]));  // open: Qn, preset, reset
  not not_40 (not_40_out, or_17_out);
  and and_129 (and_129_out, and_140_out, not_33_out);
  and and_130 (and_130_out, and_136_out, not_33_out);
  and and_131 (and_131_out, not_46_out, and_139_out);
  xor xor_7 (xor_7_out, not_41_out, and_131_out);
  and and_132 (and_132_out, not_36_out, not_37_out, not_38_out, not_39_out);
  and and_133 (and_133_out, d_ff_47_q, and_120_out, or_27_out);
  and and_134 (and_134_out, d_ff_48_q, and_122_out, or_27_out);
  Multiplexer #(.enable("false")) multiplexer_14 (
    .in0(d_ff_50_q[3]), .in1(d_ff_49_q[3]), .out(multiplexer_14_out), .sel(not_31_out));
  Multiplexer #(.width(4)) multiplexer_15 (
    .in0(d_ff_50_q), .in1(d_ff_49_q), .out(multiplexer_15_out), .sel(not_40_out));  // open: en
  and and_135 (and_135_out, multiplexer_15_out[3], or_14_out);
  and and_136 (and_136_out, multiplexer_15_out[2], or_14_out);
  and and_137 (and_137_out, and_135_out, d_ff_40_q[2]);
  and and_138 (and_138_out, and_141_out, not_33_out);
  not not_41 (not_41_out, and_137_out);
  xor xor_8 (xor_8_out, not_46_out, and_139_out);
  and and_139 (and_139_out, not_45_out, and_145_out);
  not not_42 (not_42_out, or_28_out);
  not not_43 (not_43_out, and_117_out);
  not not_44 (not_44_out, or_28_out);
  Multiplexer #(.enable("false")) multiplexer_16 (
    .in0(d_ff_50_q[2]), .in1(d_ff_49_q[2]), .out(multiplexer_16_out), .sel(not_31_out));
  and and_140 (and_140_out, multiplexer_15_out[1], or_14_out);
  and and_141 (and_141_out, multiplexer_15_out[0], or_14_out);
  and and_142 (and_142_out, and_140_out, d_ff_40_q[2]);
  and and_143 (and_143_out, and_136_out, d_ff_40_q[2]);
  and and_144 (and_144_out, and_141_out, d_ff_40_q[2]);
  not not_45 (not_45_out, and_142_out);
  not not_46 (not_46_out, and_143_out);
  not not_47 (not_47_out, and_144_out);
  xor xor_9 (xor_9_out, not_45_out, and_145_out);
  and and_145 (and_145_out, not_47_out, 1'b1);
  and Neg_2 (Neg_2_out, or_28_out, and_117_out);
  and Pos_2 (Pos_2_out, not_42_out, not_43_out);
  and and_146 (Zero, and_132_out, clock_1_out);
  or or_32 (or_32_out, and_133_out, and_134_out);
  and and_147 (and_147_out, and_120_out, not_35_out, multiplexer_16_out);
  D_Flip_Flop #(.trigger("high")) d_ff_51 (
    .D(and_147_out), .clk(and_121_out), .Q(d_ff_51_q));  // open: Qn, preset, reset
  and and_148 (and_148_out, and_122_out, not_35_out, multiplexer_16_out);
  D_Flip_Flop #(.trigger("high")) d_ff_52 (
    .D(and_148_out), .clk(and_123_out), .Q(d_ff_52_q));  // open: Qn, preset, reset
  Multiplexer #(.enable("false")) multiplexer_17 (
    .in0(d_ff_50_q[1]), .in1(d_ff_49_q[1]), .out(multiplexer_17_out), .sel(not_31_out));
  xor xor_10 (xor_10_out, not_47_out, 1'b1);
  and and_149 (and_149_out, Negative, Neg_2_out);
  and and_150 (and_150_out, Pos_2_out, Negative);
  and and_151 (and_151_out, not_48_out, not_44_out, filladder_4_c);
  not not_48 (not_48_out, d_ff_40_q[2]);
  not not_49 (not_49_out, multiplexer_5_out[3]);
  not not_50 (not_50_out, multiplexer_15_out[3]);
  or or_33 (or_33_out, and_152_out, and_153_out);
  and and_152 (and_152_out, d_ff_51_q, and_120_out, or_27_out);
  and and_153 (and_153_out, d_ff_52_q, and_122_out, or_27_out);
  Multiplexer #(.enable("false")) multiplexer_18 (
    .in0(d_ff_50_q[0]), .in1(d_ff_49_q[0]), .out(multiplexer_18_out), .sel(not_31_out));
  not not_51 (not_51_out, filladder_4_c);
  and and_154 (and_154_out, and_149_out, not_51_out);
  or or_34 (or_34_out, and_151_out, and_150_out, and_154_out);
  not not_52 (not_52_out, Zero);
  and notZero_2 (Overflow, or_34_out, not_52_out);
  or or_35 (or_35_out, and_158_out, and_159_out);
  and and_155 (SignedOverflow, Negative, not_49_out, not_50_out);
  or or_36 (or_36_out, and_162_out, and_163_out);
  and and_156 (and_156_out, and_120_out, not_35_out, multiplexer_17_out);
  D_Flip_Flop #(.trigger("high")) d_ff_53 (
    .D(and_156_out), .clk(and_121_out), .Q(d_ff_53_q));  // open: Qn, preset, reset
  D_Flip_Flop #(.trigger("high")) d_ff_54 (
    .D(and_157_out), .clk(and_123_out), .Q(d_ff_54_q));  // open: Qn, preset, reset
  and and_157 (and_157_out, and_122_out, not_35_out, multiplexer_17_out);
  and and_158 (and_158_out, d_ff_53_q, and_120_out, or_27_out);
  and and_159 (and_159_out, d_ff_54_q, and_122_out, or_27_out);
  and and_160 (and_160_out, and_120_out, not_35_out, multiplexer_18_out);
  D_Flip_Flop #(.trigger("high")) d_ff_55 (
    .D(and_160_out), .clk(and_121_out), .Q(d_ff_55_q));  // open: Qn, preset, reset
  and and_161 (and_161_out, and_122_out, not_35_out, multiplexer_18_out);
  D_Flip_Flop #(.trigger("high")) d_ff_56 (
    .D(and_161_out), .clk(and_123_out), .Q(d_ff_56_q));  // open: Qn, preset, reset
  and and_162 (and_162_out, d_ff_55_q, and_120_out, or_27_out);
  and and_163 (and_163_out, d_ff_56_q, and_122_out, or_27_out);

  assign out_22 = Negative_2;

  // Notes on the sheet:
  //   FUNDA KOK, 261052012
  //   Mode input pin
  //   0= write  /  1=read
  //   PC 
  //   Add/Sub command
  //   0 add, 1 sub
  //   4-bit instruction input pins
  //   B Input
  //   Instruction RAM
  //   Adder
  //   A Input
  //   Set 1 to stop incrementing
  //   I am using the ALU we saw as a counter that increments by 0 when program Halts
  //   2's Complement
  //   If The instruction is not HALT, increment PC
  //   IR
  //   Status output
  //   -8 + -8 is underflow (not supported)
  //   Load the value at address 0 into R0
  //   Load the value at address 1 into R0
  //   Load the value at address 0 into R1
  //   Load the value at address 1 into R1
  //   Save the value in R0 at address 0
  //   Save the value in R0 at address 1
  //   Save the value in R1 at address 0
  //   Save the value in R1 at address 1
  //   Add R0 and R0, save it in R0
  //   Add R0 and R1, save it in R0
  //   Add R1 and R0 save it in R1
  //   Add R1 and R1, save it in R1
  //   Sub R0 and R0, save it in R0
  //   Sub R0 and R1, save it in R0
  //   Sub R1 and R0, save it in R1
  //   Halt
  //   0 add, 1 sub
  //   L Initial Value
  //   B Input
  //   Address
  //   R1
  //   R0
  //   Register Block
  //   Mode input pin
  //   ALU
  //   Access to DATA RAM is allowed only when we have a load or save instruction
  //   0= write  /  1=read
  //   A Input
  //   Adder
  //   0
  //   1
  //   2's Complement
  //   Data RAM
  //   Status output
  //   -8 + -8 is underflow (not supported)
endmodule

module FillAdder (
  input  A,
  input  B,
  input  Carry,
  output C,
  output Sum
);

  wire and_1_out, and_2_out, xor_1_out;

  and and_1 (and_1_out, A, B);
  xor xor_1 (xor_1_out, A, B);
  and and_2 (and_2_out, xor_1_out, Carry);
  or or_1 (C, and_1_out, and_2_out);
  xor xor_2 (Sum, xor_1_out, Carry);
endmodule
